# Fritzing sketch charge1_01 (saved by Fritzing 0.9.2b)
breadboards: 1

parts:
  LM317 = Voltage Regulator - Variable [package="TO220 [THT]"]
  R1 = Resistor [tolerance=±5% resistance=180 package=THT]
  R2 = Resistor [tolerance=±5% resistance=560 package=THT]
  C1 = Tantalum Capacitor [capacitance=0.1mF package="100 mil [THT, tantalum]"]
  C2 = Tantalum Capacitor [capacitance=1μF package="100 mil [THT, tantalum]"]

nets:
  N1: LM317.ADJ, R1.Pin_1, R2.Pin_0
  out: LM317.OUT, R1.Pin_0, C2.+
  7.5V: LM317.IN, C1.+
  GND: R2.Pin_1, C1.-, C2.-
