# Fritzing sketch charge2_01 (saved by Fritzing 0.9.2b)
breadboards: 1

parts:
  LM317 = Voltage Regulator - Variable [package="TO220 [THT]"]
  R1 = Resistor [tolerance=±5% resistance=12.5 package=THT]
  C1 = Tantalum Capacitor [capacitance=1μF package="100 mil [THT, tantalum]"]

nets:
  out: LM317.ADJ, R1.Pin_1
  N1: LM317.OUT, R1.Pin_0
  7.5V: LM317.IN, C1.+
  GND: C1.-
