# Fritzing sketch ladeschaltung_02 (saved by Fritzing 0.9.2b)
circuit board: 8.46667cm x 5.64444cm
breadboards: 1

parts:
  Q2_IRF9640 = Basic FET P-Channel [package="TO220 [THT]"]
  Q1_2N7000 = Basic FET N-Channel [package="TO220 [THT]"]
  R1 = Resistor [tolerance=±5% resistance=4.7k package=THT]
  R2 = Resistor [tolerance=±5% resistance=4.7k package=THT]
  R3 = Resistor [tolerance=±5% resistance=12.5 package=THT]
  Akku = LIPO-1000mAh [package=lipo-1000]
  R4 = Resistor [tolerance=±5% resistance=180 package=THT]
  R5 = Resistor [tolerance=±5% resistance=560 package=THT]
  R7 = Resistor [tolerance=±5% resistance=4.7k package=THT]
  Q3_BC307 = PNP-Transistor [package="TO92 [THT]"]
  LM317 = Voltage Regulator - Variable [package="TO220 [THT]"]
  D1 = Rectifier Diode [package="300 mil [THT]"]
  R8 = Resistor [tolerance=±5% resistance=4.7k package=THT]

nets:
  N1: Q2_IRF9640.gate, Q1_2N7000.drain, R2.Pin_0
  N2: Q2_IRF9640.drain, LM317.IN
  7.5V: Q2_IRF9640.source, R2.Pin_1
  N3: Q1_2N7000.gate, R1.Pin_1
  GND: Q1_2N7000.source, Akku.-, R5.Pin_1
  IO D7: R1.Pin_0
  N4: R3.Pin_0, R4.Pin_0, LM317.OUT
  N5: R3.Pin_1, Q3_BC307.C, D1.anode
  N6: Akku.+, D1.cathode, R8.Pin_0
  N7: R4.Pin_1, R5.Pin_0, Q3_BC307.E, LM317.ADJ
  N8: R7.Pin_0, Q3_BC307.B
  IO D8: R7.Pin_1
  ADC A7: R8.Pin_1
