# Fritzing sketch schaltplan_01 (saved by Fritzing 0.9.2b)
circuit board: 8.46667cm x 5.64444cm
breadboards: 1

parts:
  Bauteil1 = Arduino Nano (Rev3.0)
  U1 = LCD-16X2 [package=lcd-16x2_noholes]
  I2C-Parallel = PCF8574 [package="DIP16 [THT]"]
  S2 = SWITCH-MOMENTARY-2 [package=tactile-pth-12mm]
  S3 = SWITCH-MOMENTARY-2 [package=tactile-pth-12mm]
  S4 = SWITCH-MOMENTARY-2 [package=tactile-pth-12mm]
  S1 = SWITCH-MOMENTARY-2 [package=tactile-pth-12mm]
  R1 = Resistor [tolerance=±5% resistance=4.7k package=THT]
  R2 = Resistor [tolerance=±5% resistance=4.7k package=THT]
  R4 = Resistor [tolerance=±5% resistance=4.7k package=THT]
  RTC = Real Time Clock Module
  R3 = Resistor [tolerance=±5% resistance=4.7k package=THT]
  18B20 = TMP36 [part_number="T Sensor" package=to-92-kit]

nets:
  GND: Bauteil1.GND, U1.VSS, I2C-Parallel.A0, I2C-Parallel.A1, I2C-Parallel.A3, I2C-Parallel.GND, R1.Pin_0, R2.Pin_0, R4.Pin_0, RTC.GND, R3.Pin_0, 18B20.GND
  N1: Bauteil1.D2, S1.2
  N2: Bauteil1.D3, S2.2
  N3: Bauteil1.D4, S3.2
  N4: Bauteil1.D5, S4.2
  N5: Bauteil1.D6, 18B20.VOUT
  Ladestrategie 2: Bauteil1.D7
  Ladestrategie 1: Bauteil1.D8
  7.5V: Bauteil1.VIN
  5V: Bauteil1.5V, U1.VDD, I2C-Parallel.VCC, RTC.5V, 18B20.VCC
  ADC Eingang: Bauteil1.A7
  N6: Bauteil1.A5, I2C-Parallel.SCL, RTC.SCL
  N7: Bauteil1.A4, I2C-Parallel.SDA, RTC.SDA
  N8: U1.DB0, I2C-Parallel.P0
  N9: U1.DB1, I2C-Parallel.P1
  N10: U1.DB2, I2C-Parallel.P2
  N11: U1.DB3, I2C-Parallel.P3
  N12: U1.DB4, I2C-Parallel.P4
  N13: U1.DB5, I2C-Parallel.P5
  N14: U1.DB6, I2C-Parallel.P6
  N15: U1.DB7, I2C-Parallel.P7
  N16: S2.1, R2.Pin_1
  N17: S3.1, R3.Pin_1
  N18: S4.1, R4.Pin_1
  N19: S1.1, R1.Pin_1

notes:
  SDA
  SCL
  IO
  ADC

custom parts:
  Real Time Clock Module: This a custom designed module for the DS1307 Real Time Clock. The module comes fully assembled and pre-programmed with the current time (ok, so it's our current time - MST). The included Lithium coin cell battery (CR1225 41mAh) will run the module for a minimum of 9 years (17 years typical) without external 5V power. The DS1307 is accessed via the I2C protocol. We've written a test-bed to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
  TMP36: Precision degC temp sensor, analog out
