# Fritzing sketch ladeschaltung_01 (saved by Fritzing 0.9.2b)
circuit board: 8.46667cm x 5.64444cm
breadboards: 1

parts:
  U1 = V_REG_LD1117VXX [package=78xxl]
  Q2 = Basic FET P-Channel [package="TO220 [THT]"]
  Q1 = Basic FET N-Channel [package="TO220 [THT]"]
  R1 = Resistor [tolerance=±5% resistance=4.7k package=THT]
  R2 = Resistor [tolerance=±5% resistance=4.7k package=THT]
  R3 = Resistor [tolerance=±5% resistance=6 package=THT]
  U2 = LIPO-1000mAh [package=lipo-1000]

nets:
  N1: U1.OUT, R3.Pin_0
  N2: U1.GND, R3.Pin_1, U2.+
  N3: U1.IN, Q2.drain
  N4: Q2.gate, Q1.drain, R2.Pin_0
  5V: Q2.source, R2.Pin_1
  N5: Q1.gate, R1.Pin_1
  GND: Q1.source, U2.-
  dig input: R1.Pin_0
